# Fritzing sketch config (saved by Fritzing 0.9.3b)
breadboards: 1

parts:
  Componente1 = Arduino Uno (Rev3) - ICSP
  U1 = ESP8266 WiFi Module [part_number=ESP8266]
  RHT1 = Humidity and Temperature Sensor RHT03

nets:
  GND: Componente1.GND, Componente1.RESET, U1.GPIO_0, U1.GND, RHT1.GND_2
  N1: Componente1.D0/RX, U1.RXD
  N2: Componente1.D1/TX, U1.TXD
  VCC: Componente1.3V3, U1.VCC, U1.CH_PD, RHT1.Vcc
  N3: U1.GPIO_2, RHT1.Data-signal

notes:
  To be able to use Arduino as a programmer,
  connect the reset to GND
  ESP-01 use 3.3V
  ESP01 PINOUT
  ° TXT ° GND
  ° CH_PD ° GPIO2
  ° RST ° GPIO0
  ° VCC ° RX
  Connect GPIO0 and GND to enter programming mode. Once the sketch is installed, disconnect it and restart the module ESP01
  CH_PD is Chip Enable connect it to VCC (3V)

custom parts:
  ESP8266 WiFi Module: Generic WiFi Module based on the ESP8266 with onboard PCB antenna and UART communications

// code stored in the sketch: Server.ino
#include <ESP8266WiFi.h>
 
const char* ssid = "********";
const char* password = "********";

int ledPin = 2; // GPIO2 of ESP8266
WiFiServer server(80);
 
void setup() {
  Serial.begin(115200);
  delay(10);
 
  pinMode(ledPin, OUTPUT);
  digitalWrite(ledPin, LOW);
   
  // Connect to WiFi network
  Serial.println();
  Serial.print("Connecting to ");
  Serial.println(ssid);

  // Static ip (Comment this block to use DHCP)
  IPAddress ip(192, 168, 1, 150);   
  IPAddress gateway(192, 168, 1, 1);   
  IPAddress subnet(255, 255, 255, 0);   
  WiFi.config(ip, gateway, subnet);

  // Inizialization Wifi 
  WiFi.begin(ssid, password);
   
  while (WiFi.status() != WL_CONNECTED) {
    delay(500);
    Serial.print(".");
  }
  
  Serial.println("");
  Serial.println("WiFi connected");
   
  // Start the server
  server.begin();
  Serial.println("Server started");
 
  // Print the IP address
  Serial.print("Use this URL to connect: ");
  Serial.print("http://");
  Serial.print(WiFi.localIP());
  Serial.println("/");
    
}
 
void loop() {
  // Check if a client has connected
  WiFiClient client = server.available();
  if (!client) {
    return;
  }
   
  // Wait until the client sends some data
  Serial.println("new client");
  while(!client.available()){
    delay(1);
  }
   
  // Read the first line of the request
  String request = client.readStringUntil('\r');
  Serial.println(request);
  client.flush();
   
  // Match the request
 
  int value = LOW;
  if (request.indexOf("/LED=ON") != -1) {
    digitalWrite(ledPin, HIGH);
    value = HIGH;
  } 
  if (request.indexOf("/LED=OFF") != -1){
    digitalWrite(ledPin, LOW);
    value = LOW;
  }
 
// Set ledPin according to the request
//digitalWrite(ledPin, value);
   
 
  // Return the response
  client.println("HTTP/1.1 200 OK");
  client.println("Content-Type: text/html");
  client.println(""); //  do not forget this one
  client.println("<!DOCTYPE HTML>");
  client.println("<html>");
   
  client.print("Led pin is now: ");
   
  if(value == HIGH) {
    client.print("On");  
  } else {
    client.print("Off");
  }
  client.println("<br><br>");
  client.println("Click <a href=\"/LED=ON\">here</a> turn the LED on pin 2 ON<br>");
  client.println("Click <a href=\"/LED=OFF\">here</a> turn the LED on pin 2 OFF<br>");
  client.println("</html>");
 
  delay(1);
  Serial.println("Client disonnected");
  Serial.println("");
 
}
